// Logisim project div-100.circ as structural Verilog: 7 circuits, main circuit main
module main (
  output SDT1,
  output SDT2
);

  wire A1, A2, B1, B2, C1, C2, clock_1_out, CNTR_DIV_10_A_out1, CNTR_DIV_10_A_out2, CNTR_DIV_10_A_out4,
       CNTR_DIV_10_A_out8, CNTR_DIV_10_B_out1, CNTR_DIV_10_B_out2, CNTR_DIV_10_B_out4, CNTR_DIV_10_B_out8,
       D1, D2, E1, E2, F1, F2, G1, G2, RCO;

  Clock clock_1 (.out(clock_1_out));
  AsyncDecadeCounterDff CNTR_DIV_10_A (
    .Clk(clock_1_out), .Out1(CNTR_DIV_10_A_out1), .Out2(CNTR_DIV_10_A_out2), .Out4(CNTR_DIV_10_A_out4),
    .Out8(CNTR_DIV_10_A_out8), .RCO(RCO));  // open: RST, TC
  AsyncDecadeCounterDff CNTR_DIV_10_B (
    .Clk(RCO), .Out1(CNTR_DIV_10_B_out1), .Out2(CNTR_DIV_10_B_out2), .Out4(CNTR_DIV_10_B_out4),
    .Out8(CNTR_DIV_10_B_out8));  // open: RST, TC, RCO
  BinTo7SegMUX binto7segmux_1 (
    .Clk(clock_1_out), .In1(CNTR_DIV_10_A_out1), .In2(CNTR_DIV_10_A_out2), .In4(CNTR_DIV_10_A_out4),
    .In8(CNTR_DIV_10_A_out8), .SO4(SDT1), .A(A1), .B(B1), .C(C1), .D(D1), .E(E1), .F(F1), .G(G1));  // open: SO1, SO2, SDT
  BinTo7SegMUX binto7segmux_2 (
    .Clk(RCO), .In1(CNTR_DIV_10_B_out1), .In2(CNTR_DIV_10_B_out2), .In4(CNTR_DIV_10_B_out4),
    .In8(CNTR_DIV_10_B_out8), .SDT(SDT2), .A(A2), .B(B2), .C(C2), .D(D2), .E(E2), .F(F2), .G(G2));  // open: SO1, SO2, SO4
  _7_Segment_Display #(.decimalPoint("false")) SEG2 (.g(G2), .f(F2), .a(A2), .b(B2), .e(E2), .d(D2), .c(C2));
  _7_Segment_Display #(.decimalPoint("false")) SEG1 (.g(G1), .f(F1), .a(A1), .b(B1), .e(E1), .d(D1), .c(C1));

  // Notes on the sheet:
  //   => Clock input (Clk) can be driven by a sensor to count items.
  //   => Counter decoding can be used to detect when at a specific count.
  //   => Terminal Count output (TC) can be used to trigger an action when done counting.
  //   => Ripple clock output (RCO) for counter B can be used to drive another counter to achieve higher modulus.
endmodule

module AsyncDecadeCounter (
  input  Vcc,
  input  Clk,
  output Out1,
  output Out2,
  output Out4,
  output Out8,
  output TC,
  output RCO
);

  wire and_1_out, j_k_ff_1_qn, j_k_ff_2_qn, j_k_ff_3_qn;

  J_K_Flip_Flop j_k_ff_1 (.J(Vcc), .K(Vcc), .clk(Clk), .Q(Out1), .Qn(j_k_ff_1_qn), .reset(and_1_out));  // open: preset
  J_K_Flip_Flop j_k_ff_2 (
    .J(Vcc), .K(Vcc), .clk(j_k_ff_1_qn), .Q(Out2), .Qn(j_k_ff_2_qn), .reset(and_1_out));  // open: preset
  J_K_Flip_Flop j_k_ff_3 (
    .J(Vcc), .K(Vcc), .clk(j_k_ff_2_qn), .Q(Out4), .Qn(j_k_ff_3_qn), .reset(and_1_out));  // open: preset
  J_K_Flip_Flop j_k_ff_4 (.J(Vcc), .K(Vcc), .clk(j_k_ff_3_qn), .Q(Out8), .Qn(RCO), .reset(and_1_out));  // open: preset
  and and_1 (and_1_out, Out2, Out8);
  and and_2 (TC, Out1, Out8);
endmodule

module FourToNineLine (
  input  In1,
  input  In2,
  input  In4,
  input  In8,
  output Out0,
  output Out1,
  output Out2,
  output Out3,
  output Out4,
  output Out5,
  output Out6,
  output Out7,
  output Out8,
  output Out9
);

  wire not_1_out, not_2_out, not_3_out, not_4_out;

  not not_1 (not_1_out, In1);
  not not_2 (not_2_out, In2);
  not not_3 (not_3_out, In4);
  not not_4 (not_4_out, In8);
  and and_1 (Out0, not_1_out, not_2_out, not_3_out, not_4_out);
  and and_2 (Out1, In1, not_2_out, not_3_out, not_4_out);
  and and_3 (Out2, not_1_out, In2, not_3_out, not_4_out);
  and and_4 (Out3, In1, In2, not_3_out, not_4_out);
  and and_5 (Out4, not_1_out, not_2_out, In4, not_4_out);
  and and_6 (Out5, In1, not_2_out, In4, not_4_out);
  and and_7 (Out6, not_1_out, In2, In4, not_4_out);
  and and_8 (Out7, In1, In2, In4, not_4_out);
  and and_9 (Out8, not_1_out, In8);
  and and_10 (Out9, In1, In8);
endmodule

module BinTo7Seg (
  input  In1,
  input  In2,
  input  In4,
  input  In8,
  output A,
  output B,
  output C,
  output D,
  output E,
  output F,
  output G
);

  wire BIN_TO_DEC_out0, BIN_TO_DEC_out1, BIN_TO_DEC_out2, BIN_TO_DEC_out3, BIN_TO_DEC_out4, BIN_TO_DEC_out5,
       BIN_TO_DEC_out6, BIN_TO_DEC_out7, BIN_TO_DEC_out8, BIN_TO_DEC_out9, or_1_out, or_3_out;

  FourToNineLine BIN_TO_DEC (
    .In1(In1), .In2(In2), .In4(In4), .In8(In8), .Out0(BIN_TO_DEC_out0), .Out1(BIN_TO_DEC_out1),
    .Out2(BIN_TO_DEC_out2), .Out3(BIN_TO_DEC_out3), .Out4(BIN_TO_DEC_out4), .Out5(BIN_TO_DEC_out5),
    .Out6(BIN_TO_DEC_out6), .Out7(BIN_TO_DEC_out7), .Out8(BIN_TO_DEC_out8), .Out9(BIN_TO_DEC_out9));
  or or_1 (or_1_out, BIN_TO_DEC_out0, BIN_TO_DEC_out2, BIN_TO_DEC_out3, BIN_TO_DEC_out5, BIN_TO_DEC_out6, BIN_TO_DEC_out7, BIN_TO_DEC_out8);
  or or_2 (B, BIN_TO_DEC_out0, BIN_TO_DEC_out1, BIN_TO_DEC_out2, BIN_TO_DEC_out3, BIN_TO_DEC_out7, BIN_TO_DEC_out8, BIN_TO_DEC_out9);
  or or_3 (or_3_out, BIN_TO_DEC_out0, BIN_TO_DEC_out1, BIN_TO_DEC_out3, BIN_TO_DEC_out4, BIN_TO_DEC_out5, BIN_TO_DEC_out6, BIN_TO_DEC_out7);
  or or_4 (D, BIN_TO_DEC_out0, BIN_TO_DEC_out2, BIN_TO_DEC_out3, BIN_TO_DEC_out4, BIN_TO_DEC_out5, BIN_TO_DEC_out6, BIN_TO_DEC_out8);
  or or_5 (E, BIN_TO_DEC_out0, BIN_TO_DEC_out2, BIN_TO_DEC_out4, BIN_TO_DEC_out6, BIN_TO_DEC_out8);
  or or_6 (F, BIN_TO_DEC_out0, BIN_TO_DEC_out4, BIN_TO_DEC_out5, BIN_TO_DEC_out6, BIN_TO_DEC_out8, BIN_TO_DEC_out9);
  or or_7 (G, BIN_TO_DEC_out2, BIN_TO_DEC_out3, BIN_TO_DEC_out5, BIN_TO_DEC_out6, BIN_TO_DEC_out8, BIN_TO_DEC_out9);
  or or_8 (A, or_1_out, BIN_TO_DEC_out9);
  or or_9 (C, or_3_out, BIN_TO_DEC_out8, BIN_TO_DEC_out9);
endmodule

module AsyncDecadeCounterDff (
  input  Clk,
  input  RST,
  output Out1,
  output Out2,
  output Out4,
  output Out8,
  output TC,
  output RCO
);

  wire and_1_out, d_ff_1_qn, d_ff_2_qn, d_ff_3_qn, d_ff_4_qn, or_1_out;

  D_Flip_Flop #(.trigger("falling")) d_ff_1 (
    .D(d_ff_1_qn), .clk(Clk), .Q(Out1), .Qn(d_ff_1_qn), .reset(or_1_out));  // open: preset
  D_Flip_Flop #(.trigger("falling")) d_ff_2 (
    .D(d_ff_2_qn), .clk(Out1), .Q(Out2), .Qn(d_ff_2_qn), .reset(or_1_out));  // open: preset
  D_Flip_Flop #(.trigger("falling")) d_ff_3 (
    .D(d_ff_3_qn), .clk(Out2), .Q(Out4), .Qn(d_ff_3_qn), .reset(or_1_out));  // open: preset
  D_Flip_Flop #(.trigger("falling")) d_ff_4 (
    .D(d_ff_4_qn), .clk(Out4), .Q(Out8), .Qn(d_ff_4_qn), .reset(or_1_out));  // open: preset
  or or_1 (or_1_out, and_1_out, RST);
  and and_1 (and_1_out, Out2, Out8);
  and and_2 (TC, Out1, Out8);

  assign RCO = Out8;
endmodule

module OneOfSeven (
  input  S1,
  input  S2,
  input  S4,
  input  InA,
  input  InB,
  input  InC,
  input  InD,
  input  InE,
  input  InF,
  input  InG,
  output SO1,
  output SO2,
  output SO4,
  output SDT
);

  wire and_1_out, and_2_out, and_3_out, and_4_out, and_5_out, and_6_out, and_7_out, not_1_out, not_2_out,
       not_3_out;

  not not_1 (not_1_out, S1);
  not not_2 (not_2_out, S2);
  not not_3 (not_3_out, S4);
  and and_1 (and_1_out, not_1_out, not_2_out, not_3_out, InA);
  and and_2 (and_2_out, S1, not_2_out, not_3_out, InB);
  and and_3 (and_3_out, not_1_out, S2, not_3_out, InC);
  and and_4 (and_4_out, S1, S2, not_3_out, InD);
  and and_5 (and_5_out, not_1_out, not_2_out, S4, InE);
  and and_6 (and_6_out, S1, not_2_out, S4, InF);
  and and_7 (and_7_out, S2, S4, InG);
  or or_1 (SDT, and_1_out, and_2_out, and_3_out, and_4_out, and_5_out, and_6_out, and_7_out);

  assign SO1 = S1;
  assign SO2 = S2;
  assign SO4 = S4;
endmodule

module BinTo7SegMUX (
  input  Clk,
  input  In1,
  input  In2,
  input  In4,
  input  In8,
  output SO1,
  output SO2,
  output SO4,
  output SDT,
  output A,
  output B,
  output C,
  output D,
  output E,
  output F,
  output G
);

  wire and_1_out, asyncdecadecounterdff_1_out1, asyncdecadecounterdff_1_out2, asyncdecadecounterdff_1_out4;

  AsyncDecadeCounterDff asyncdecadecounterdff_1 (
    .Clk(Clk), .RST(and_1_out), .Out1(asyncdecadecounterdff_1_out1), .Out2(asyncdecadecounterdff_1_out2),
    .Out4(asyncdecadecounterdff_1_out4));  // open: Out8, TC, RCO
  BinTo7Seg binto7seg_1 (.In1(In1), .In2(In2), .In4(In4), .In8(In8), .A(A), .B(B), .C(C), .D(D), .E(E), .F(F), .G(G));
  and and_1 (and_1_out, asyncdecadecounterdff_1_out1, asyncdecadecounterdff_1_out2, asyncdecadecounterdff_1_out4);
  OneOfSeven oneofseven_1 (
    .S1(asyncdecadecounterdff_1_out1), .S2(asyncdecadecounterdff_1_out2), .S4(asyncdecadecounterdff_1_out4),
    .InA(A), .InB(B), .InC(C), .InD(D), .InE(E), .InF(F), .InG(G), .SO1(SO1), .SO2(SO2), .SO4(SO4), .SDT(SDT));
endmodule
