// Logisim project div-16.circ as structural Verilog: 7 circuits, main circuit main
module main (
);

  wire A, B, C, clock_1_out, D, E, F, fourbitasynccounter_1_q0, fourbitasynccounter_1_q1,
       fourbitasynccounter_1_q2, fourbitasynccounter_1_q3, fourtosixteenline_1_out0,
       fourtosixteenline_1_out1, fourtosixteenline_1_out2, fourtosixteenline_1_out3,
       fourtosixteenline_1_out4, fourtosixteenline_1_out5, fourtosixteenline_1_out6,
       fourtosixteenline_1_out7, fourtosixteenline_1_out8, fourtosixteenline_1_out9,
       fourtosixteenline_1_out10, fourtosixteenline_1_out11, fourtosixteenline_1_out12,
       fourtosixteenline_1_out13, fourtosixteenline_1_out14, fourtosixteenline_1_out15, G, Out0, Out1, Out2,
       Out3, Out4, Out5, Out10, Out11, Out12, Out13, Out14, Out15, pull_resistor_1_node,
       pull_resistor_2_node, YA, YB, YC, YD, YE, YF, YG;

  Clock clock_1 (.out(clock_1_out));
  Pull_Resistor pull_resistor_1 (.node(pull_resistor_1_node));
  Pull_Resistor pull_resistor_2 (.node(pull_resistor_2_node));
  FourBitAsyncCounter fourbitasynccounter_1 (
    .Clk(clock_1_out), .Vcc(1'b1), .Q0(fourbitasynccounter_1_q0), .Q1(fourbitasynccounter_1_q1),
    .Q2(fourbitasynccounter_1_q2), .Q3(fourbitasynccounter_1_q3), .TC(pull_resistor_2_node),
    .RCO(pull_resistor_1_node));
  FourToSixteenLine fourtosixteenline_1 (
    .In0(fourbitasynccounter_1_q0), .In1(fourbitasynccounter_1_q1), .In2(fourbitasynccounter_1_q2),
    .In3(fourbitasynccounter_1_q3), .Out0(fourtosixteenline_1_out0), .Out1(fourtosixteenline_1_out1),
    .Out2(fourtosixteenline_1_out2), .Out3(fourtosixteenline_1_out3), .Out4(fourtosixteenline_1_out4),
    .Out5(fourtosixteenline_1_out5), .Out10(fourtosixteenline_1_out10), .Out11(fourtosixteenline_1_out11),
    .Out12(fourtosixteenline_1_out12), .Out13(fourtosixteenline_1_out13), .Out14(fourtosixteenline_1_out14),
    .Out15(fourtosixteenline_1_out15), .Out6(fourtosixteenline_1_out6), .Out7(fourtosixteenline_1_out7),
    .Out8(fourtosixteenline_1_out8), .Out9(fourtosixteenline_1_out9));
  Overflow15 overflow15_1 (
    .In10(Out10), .In11(Out11), .In12(Out12), .In13(Out13), .In14(Out14), .In15(Out15), .A(YA), .B(YB),
    .C(YC), .D(YD), .E(YE), .F(YF), .G(YG));
  TwelveToSixOR twelvetosixor_1 (
    .In0(fourtosixteenline_1_out0), .In1(fourtosixteenline_1_out1), .In2(fourtosixteenline_1_out2),
    .In3(fourtosixteenline_1_out3), .In4(fourtosixteenline_1_out4), .In5(fourtosixteenline_1_out5),
    .In10(fourtosixteenline_1_out10), .In11(fourtosixteenline_1_out11), .In12(fourtosixteenline_1_out12),
    .In13(fourtosixteenline_1_out13), .In14(fourtosixteenline_1_out14), .In15(fourtosixteenline_1_out15),
    .Out0(Out0), .Ou1(Out1), .Ou2(Out2), .Out3(Out3), .Out4(Out4), .Out5(Out5), .Out10(Out10), .Out11(Out11),
    .Out12(Out12), .Out13(Out13), .Out14(Out14), .Out15(Out15));
  _7_Segment_Display u_7_segment_display_1 (.g(YG), .f(YF), .a(YA), .b(YB), .e(YE), .d(YD), .c(YC));  // open: dp
  DecTo7Seg decto7seg_1 (
    .In0(Out0), .In1(Out1), .In2(Out2), .In3(Out3), .In4(Out4), .In5(Out5), .In6(fourtosixteenline_1_out6),
    .In7(fourtosixteenline_1_out7), .In8(fourtosixteenline_1_out8), .In9(fourtosixteenline_1_out9), .A(A),
    .B(B), .C(C), .D(D), .E(E), .F(F), .G(G));
  _7_Segment_Display u_7_segment_display_2 (.g(G), .f(F), .a(A), .b(B), .e(E), .d(D), .c(C));  // open: dp
endmodule

module TwoBitAsyncCntr (
  input  Clk,
  input  Vcc,
  output Q0,
  output Q1,
  output TC,
  output RCO
);

  wire j_k_ff_1_qn;

  J_K_Flip_Flop j_k_ff_1 (.J(Vcc), .K(Vcc), .clk(Clk), .Q(Q0), .Qn(j_k_ff_1_qn));  // open: preset, reset
  J_K_Flip_Flop j_k_ff_2 (.J(Vcc), .K(Vcc), .clk(j_k_ff_1_qn), .Q(Q1), .Qn(RCO));  // open: preset, reset
  and and_1 (TC, Q0, Q1);
endmodule

module FourBitAsyncCounter (
  input  Clk,
  input  Vcc,
  output Q0,
  output Q1,
  output Q2,
  output Q3,
  output TC,
  output RCO
);

  wire twobitasynccntr_1_rco, twobitasynccntr_1_tc, twobitasynccntr_2_tc;

  TwoBitAsyncCntr twobitasynccntr_1 (
    .Clk(Clk), .Vcc(Vcc), .Q0(Q0), .Q1(Q1), .TC(twobitasynccntr_1_tc), .RCO(twobitasynccntr_1_rco));
  TwoBitAsyncCntr twobitasynccntr_2 (
    .Clk(twobitasynccntr_1_rco), .Vcc(Vcc), .Q0(Q2), .Q1(Q3), .TC(twobitasynccntr_2_tc), .RCO(RCO));
  and and_1 (TC, twobitasynccntr_1_tc, twobitasynccntr_2_tc);
endmodule

module FourToSixteenLine (
  input  In0,
  input  In1,
  input  In2,
  input  In3,
  output Out0,
  output Out1,
  output Out2,
  output Out3,
  output Out4,
  output Out5,
  output Out10,
  output Out11,
  output Out12,
  output Out13,
  output Out14,
  output Out15,
  output Out6,
  output Out7,
  output Out8,
  output Out9
);

  wire not_1_out, not_2_out, not_3_out, not_4_out;

  not not_1 (not_1_out, In0);
  not not_2 (not_2_out, In1);
  not not_3 (not_3_out, In2);
  not not_4 (not_4_out, In3);
  and and_1 (Out0, not_1_out, not_2_out, not_3_out, not_4_out);
  and and_2 (Out1, In0, not_2_out, not_3_out, not_4_out);
  and and_3 (Out2, not_1_out, In1, not_3_out, not_4_out);
  and and_4 (Out3, In0, In1, not_3_out, not_4_out);
  and and_5 (Out4, not_1_out, not_2_out, In2, not_4_out);
  and and_6 (Out5, In0, not_2_out, In2, not_4_out);
  and and_7 (Out6, not_1_out, In1, In2, not_4_out);
  and and_8 (Out7, In0, In1, In2, not_4_out);
  and and_9 (Out8, not_1_out, not_2_out, not_3_out, In3);
  and and_10 (Out9, In0, not_2_out, not_3_out, In3);
  and and_11 (Out10, not_1_out, In1, not_3_out, In3);
  and and_12 (Out11, In0, In1, not_3_out, In3);
  and and_13 (Out12, not_1_out, not_2_out, In2, In3);
  and and_14 (Out13, In0, not_2_out, In2, In3);
  and and_15 (Out14, not_1_out, In1, In2, In3);
  and and_16 (Out15, In0, In1, In2, In3);
endmodule

module DecTo7Seg (
  input  In0,
  input  In1,
  input  In2,
  input  In3,
  input  In4,
  input  In5,
  input  In6,
  input  In7,
  input  In8,
  input  In9,
  output A,
  output B,
  output C,
  output D,
  output E,
  output F,
  output G
);

  wire or_1_out, or_2_out, or_3_out, or_4_out, or_6_out, or_7_out;

  or or_1 (or_1_out, In0, In2, In3, In5, In6);
  or or_2 (or_2_out, In0, In1, In2, In3, In7);
  or or_3 (or_3_out, In0, In1, In3, In4, In5);
  or or_4 (or_4_out, In0, In2, In3, In4, In5);
  or or_5 (E, In0, In2, In4, In6, In8);
  or or_6 (or_6_out, In0, In4, In5, In6, In8);
  or or_7 (or_7_out, In2, In3, In5, In6, In8);
  or or_8 (A, or_1_out, In7, In8, In9);
  or or_9 (B, or_2_out, In8, In9);
  or or_10 (C, or_3_out, In6, In7, In8, In9);
  or or_11 (D, or_4_out, In6, In8);
  or or_12 (F, or_6_out, In9);
  or or_13 (G, or_7_out, In9);
endmodule

module Overflow15 (
  input  In10,
  input  In11,
  input  In12,
  input  In13,
  input  In14,
  input  In15,
  output A,
  output B,
  output C,
  output D,
  output E,
  output F,
  output G
);

  wire and_1_out, not_1_out, not_2_out, not_3_out, not_4_out, not_5_out, not_6_out, not_7_out;

  not not_1 (not_1_out, In10);
  not not_2 (not_2_out, In11);
  not not_3 (not_3_out, In12);
  not not_4 (not_4_out, In13);
  not not_5 (not_5_out, In14);
  not not_6 (not_6_out, In15);
  and and_1 (and_1_out, not_1_out, not_2_out, not_3_out, not_4_out, not_5_out, not_6_out);
  not not_7 (not_7_out, and_1_out);
  DecTo7Seg decto7seg_1 (
    .In0(and_1_out), .In1(not_7_out), .A(A), .B(B), .C(C), .D(D), .E(E), .F(F), .G(G));  // open: In2, In3, In4, In5, In6, In7, In8, In9
endmodule

module TwelveToSixOR (
  input  In0,
  input  In1,
  input  In2,
  input  In3,
  input  In4,
  input  In5,
  input  In10,
  input  In11,
  input  In12,
  input  In13,
  input  In14,
  input  In15,
  output Out0,
  output Ou1,
  output Ou2,
  output Out3,
  output Out4,
  output Out5,
  output Out10,
  output Out11,
  output Out12,
  output Out13,
  output Out14,
  output Out15
);

  or or_1 (Out0, In0, In10);
  or or_2 (Ou1, In1, In11);
  or or_3 (Ou2, In2, In12);
  or or_4 (Out3, In3, In13);
  or or_5 (Out4, In4, In14);
  or or_6 (Out5, In5, In15);

  assign Out10 = In10;
  assign Out11 = In11;
  assign Out12 = In12;
  assign Out13 = In13;
  assign Out14 = In14;
  assign Out15 = In15;
endmodule
